// Logisim project ControlUnit.circ as structural Verilog: 1 circuit, main circuit Control Unit
module Control_Unit (
  output [9:0] out_1
);

  wire clock_1_out;
  wire [9:0] PC_p3;

  Clock clock_1 (.out(clock_1_out));
  // _10BitRegister PC: pin names not known; wires that end beside it: clock_1_out, 1'b1, PC_p3, out_1
  _10BitIncrementer u_10bitincrementer_1 (.I(out_1), .O(PC_p3));

  // Notes on the sheet:
  //   out_1: pull=down
endmodule
